# Fritzing sketch relé e conversor AD com potenciometros (saved by Fritzing 0.9.3b)
breadboards: 1

parts:
  Componente1 = Arduino Uno (Rev3)
  Componente2 = Adafruit ADS1115 16Bit I2C ADC [part_number="Adafruit #1085"]
  Componente3 = songle relay
  R1 = Resistor [tolerance=±5% resistance=220 package=THT]
  R2 = Resistor [tolerance=±5% resistance=220 package=THT]
  U1 = POT [package=pot_mammoth]
  U2 = POT [package=pot_mammoth]

nets:
  N1: Componente1.A4/SDA, Componente2.SDA
  N2: Componente1.A5/SCL, Componente2.SCL
  N3: Componente1.D11_PWM/MOSI, Componente3.VCC
  GND: Componente1.GND, Componente3.GND
  5V: Componente1.5V, Componente2.VDD
  N4: Componente2.AIN0, R1.Pin_1, R2.Pin_0
  N5: Componente2.ADDR, Componente2.GND, R1.Pin_0, U1.S, U2.S
  N6: R2.Pin_1, U2.A
  N7: U1.A, U2.E

notes:
  Câmera
  12V
  0V

custom parts:
  Adafruit ADS1115 16Bit I2C ADC: For microcontrollers without an analog-to-digital converter or when you want a higher-precision ADC, the ADS1115 provides 16-bit precision at 860 samples/second over I2C. The chip can be configured as 4 single-ended input channels, or two differential channels. As a nice bonus, it even includes a programmable gain amplifier, up to x16, to help boost up smaller single/differential signals to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
